# Fritzing sketch AlarmPI_fritzing (saved by Fritzing 0.9.3b)

parts:
  Relay = Keyes Relay [package=THT]
  Raspberry_Pi_1 = Raspberry Pi 3 [part_number=RPI-3-V1.2]
  Magnetic_Sensor_1 = Magnetic Door Switch [package=reed_switch_plastic]
  Magnetic_Sensor_2 = Magnetic Door Switch [package=reed_switch_plastic]
  Serene = Piezo Speaker
  12V_DC = Power plug

nets:
  N1: Relay.signal, Raspberry_Pi_1.GPIO14
  N2: Relay.power, Raspberry_Pi_1.5V
  N3: Relay.ground, Raspberry_Pi_1.GPIO15
  N4: Relay.NC, Serene.pin1
  N5: Relay.C, 12V_DC.VCC
  N6: Raspberry_Pi_1.GND, Magnetic_Sensor_1.1, Magnetic_Sensor_2.1
  N7: Raspberry_Pi_1.GPIO12, Magnetic_Sensor_2.2
  N8: Raspberry_Pi_1.GPIO24, Magnetic_Sensor_1.2
  N9: Serene.pin2, 12V_DC.GND

custom parts:
  Keyes Relay: The Keyes 5V relay module is suitable for SCM development, home appliance control. It uses a 5V~12V TIL control signal which can control DC / AC signal.
